// Logisim project 8bitcomputer.circ as structural Verilog
module _4_bit__carry_fast (
  input  A0,
  input  A1,
  input  A2,
  input  A3,
  input  B0,
  input  B1,
  input  B2,
  input  B3,
  input  C0,
  output S0,
  output C1,
  output S1,
  output C2,
  output S2,
  output C3,
  output S3,
  output C4
);

  wire and_1_out, and_2_out, and_3_out, and_4_out, and_5_out, and_6_out, and_7_out, and_8_out, xor_2_out,
       xor_4_out, xor_6_out, xor_8_out;

  xor xor_1 (S0, C0, xor_2_out);
  xor xor_2 (xor_2_out, A0, B0);
  and and_1 (and_1_out, A0, B0);
  and and_2 (and_2_out, xor_2_out, C0);
  or or_1 (C1, and_2_out, and_1_out);
  xor xor_3 (S1, C1, xor_4_out);
  xor xor_4 (xor_4_out, A1, B1);
  and and_3 (and_3_out, A1, B1);
  and and_4 (and_4_out, xor_4_out, C1);
  or or_2 (C2, and_4_out, and_3_out);
  xor xor_5 (S2, C2, xor_6_out);
  xor xor_6 (xor_6_out, A2, B2);
  and and_5 (and_5_out, A2, B2);
  and and_6 (and_6_out, xor_6_out, C2);
  or or_3 (C3, and_6_out, and_5_out);
  xor xor_7 (S3, C3, xor_8_out);
  xor xor_8 (xor_8_out, A3, B3);
  and and_7 (and_7_out, A3, B3);
  and and_8 (and_8_out, xor_8_out, C3);
  or or_4 (C4, and_8_out, and_7_out);

  // Notes on the sheet:
  //   A
  //   B
  //   S0
  //   C1
  //   S1
  //   C2
  //   S2
  //   C3
  //   S3
  //   C4
endmodule

module full__adder (
  input  A,
  input  B,
  input  Cin,
  output S,
  output Co
);

  wire and_1_out, and_2_out, and_3_out, and_4_out, and_5_out, and_6_out, not_1_out, not_2_out, not_3_out,
       not_4_out, or_1_out;

  not not_1 (not_1_out, B);
  not not_2 (not_2_out, A);
  and and_1 (and_1_out, not_1_out, A);
  and and_2 (and_2_out, B, not_2_out);
  or or_1 (or_1_out, and_1_out, and_2_out);
  and and_3 (and_3_out, A, B);
  not not_3 (not_3_out, Cin);
  not not_4 (not_4_out, or_1_out);
  and and_4 (and_4_out, Cin, or_1_out);
  and and_5 (and_5_out, not_3_out, or_1_out);
  and and_6 (and_6_out, not_4_out, Cin);
  or or_2 (Co, and_4_out, and_3_out);
  or or_3 (S, and_5_out, and_6_out);

  // Notes on the sheet:
  //   A
  //   B
  //   Cin
  //   S
  //   Co
endmodule

module alu (
  input  A0,
  input  A1,
  input  A2,
  input  A3,
  input  A4,
  input  A5,
  input  A6,
  input  A7,
  input  B0,
  input  B1,
  input  B2,
  input  B3,
  input  B4,
  input  B5,
  input  B6,
  input  B7,
  input  in_17
);

  wire n4_bit_carry_fast_1_c4, n4_bit_carry_fast_1_s0, n4_bit_carry_fast_1_s1, n4_bit_carry_fast_1_s2,
       n4_bit_carry_fast_1_s3, n4_bit_carry_fast_2_s0, n4_bit_carry_fast_2_s1, n4_bit_carry_fast_2_s2,
       n4_bit_carry_fast_2_s3, xor_1_out, xor_2_out, xor_3_out, xor_4_out, xor_5_out, xor_6_out, xor_7_out,
       xor_8_out;

  xor xor_1 (xor_1_out, in_17, B0);
  xor xor_2 (xor_2_out, in_17, B1);
  xor xor_3 (xor_3_out, in_17, B2);
  xor xor_4 (xor_4_out, in_17, B3);
  xor xor_5 (xor_5_out, in_17, B4);
  xor xor_6 (xor_6_out, in_17, B5);
  xor xor_7 (xor_7_out, in_17, B6);
  xor xor_8 (xor_8_out, in_17, B7);
  _4_bit__carry_fast u_4_bit_carry_fast_1 (
    .A0(A0), .A1(A1), .A2(A2), .A3(A3), .B0(xor_1_out), .B1(xor_2_out), .B2(xor_3_out), .B3(xor_4_out),
    .S0(n4_bit_carry_fast_1_s0), .S1(n4_bit_carry_fast_1_s1), .S2(n4_bit_carry_fast_1_s2),
    .S3(n4_bit_carry_fast_1_s3), .C4(n4_bit_carry_fast_1_c4));  // open: C0, C1, C2, C3
  _4_bit__carry_fast u_4_bit_carry_fast_2 (
    .A0(A4), .A1(A5), .A2(A6), .A3(A7), .B0(xor_5_out), .B1(xor_6_out), .B2(xor_7_out), .B3(xor_8_out),
    .C0(n4_bit_carry_fast_1_c4), .S0(n4_bit_carry_fast_2_s0), .S1(n4_bit_carry_fast_2_s1),
    .S2(n4_bit_carry_fast_2_s2), .S3(n4_bit_carry_fast_2_s3));  // open: C1, C2, C3, C4
endmodule
